// Logisim project battleship.circ as structural Verilog: 4 circuits, main circuit main
module main (
  input  [3:0] Navio1,
  input  [3:0] Navio2,
  input  Coluna,
  input  [1:0] Linha,
  output out_5,
  output out_6
);

  wire [3:0] undriven;

  MUX mux_1 (.in_1(Navio1), .in_2(undriven), .out_3(out_5));
  MUX mux_2 (.in_1(Navio2), .in_2(undriven), .out_3(out_6));
endmodule

module decodificador (
  input  [3:0] in_1,
  output [3:0] out_2
);

  wire and_1_out, and_2_out, and_3_out, and_4_out, and_5_out, and_6_out, and_7_out, and_8_out, and_9_out;

  and and_1 (and_1_out, ~in_1[3], ~in_1[2]);  // AND_Gate
  and and_2 (and_2_out, ~in_1[2], ~in_1[1], ~in_1[0]);  // AND_Gate
  and and_3 (and_3_out, ~in_1[2], in_1[1], in_1[0]);  // AND_Gate
  and and_4 (and_4_out, in_1[3], in_1[2], ~in_1[1]);  // AND_Gate
  and and_5 (and_5_out, ~in_1[3], in_1[2], in_1[1]);  // AND_Gate
  and and_6 (and_6_out, in_1[2], in_1[1], ~in_1[0]);  // AND_Gate
  and and_7 (and_7_out, in_1[3], ~in_1[2], ~in_1[1], in_1[0]);  // AND_Gate
  and and_8 (and_8_out, ~in_1[3], in_1[2], ~in_1[1], in_1[0]);  // AND_Gate
  and and_9 (and_9_out, in_1[3], in_1[2], in_1[1], in_1[0]);
  and and_10 (out_2[3], in_1[3], ~in_1[2], in_1[1], ~in_1[0]);  // AND_Gate
  or or_1 (out_2[0], and_1_out, and_2_out, and_3_out, and_4_out);
  or or_2 (out_2[1], and_5_out, and_6_out, and_7_out);
  or or_3 (out_2[2], and_8_out, and_9_out);
endmodule

module Encoder (
  input  [3:0] Navio,
  output out_2,
  output out_3,
  output out_4,
  output out_5
);

  wire and_3_out, and_4_out, and_5_out, and_6_out, and_7_out, and_8_out, not_1_out, not_2_out, not_3_out,
       not_4_out;

  not not_1 (not_1_out, Navio[3]);
  not not_2 (not_2_out, Navio[2]);
  not not_3 (not_3_out, Navio[1]);
  not not_4 (not_4_out, Navio[0]);
  and and_1 (out_2, Navio[3], Navio[2], not_3_out, not_4_out);
  and and_2 (out_3, Navio[3], Navio[1], Navio[0]);
  and and_3 (and_3_out, not_1_out, not_2_out, not_4_out);
  and and_4 (and_4_out, not_1_out, Navio[2], Navio[0]);
  and and_5 (and_5_out, not_1_out, not_2_out, Navio[0]);
  and and_6 (and_6_out, not_1_out, Navio[2], not_4_out);
  and and_7 (and_7_out, Navio[3], not_3_out, Navio[0]);
  and and_8 (and_8_out, Navio[3], Navio[1], not_4_out);
  or or_1 (out_4, and_3_out, and_4_out);
  or or_2 (out_5, and_5_out, and_6_out, and_7_out, and_8_out);
endmodule

module MUX (
  input  [3:0] in_1,
  input  [3:0] in_2,
  output out_3
);

  wire encoder_1_out_2, encoder_1_out_3, encoder_1_out_4, encoder_1_out_5;

  Encoder encoder_1 (
    .Navio(in_1), .out_2(encoder_1_out_2), .out_3(encoder_1_out_3), .out_4(encoder_1_out_4),
    .out_5(encoder_1_out_5));
  Multiplexer #(.select(2)) multiplexer_1 (
    .in0(encoder_1_out_2), .in1(encoder_1_out_3), .in2(encoder_1_out_4), .in3(encoder_1_out_5), .out(out_3),
    .sel(in_2[1:0]));
  // Pins of 2 and 4 bits meet at in_2
endmodule
